# Fritzing sketch task 6 (saved by Fritzing 0.9.3b)
breadboards: 1

parts:
  RELAY_(5V) = Keyes Relay [package=THT]
  Nodemcu_board = NodeMCU V3.0
  5v_(Relay_input) = 4 x AAA Battery Mount
  AC_Lamp = LEDs [package=led10mm]
  AC_switch = SWITCH-MOMENTARY-2 [package=tactile-switch-1101ne]

nets:
  N1: RELAY_(5V).signal, 5v_(Relay_input).-
  N2: RELAY_(5V).power, Nodemcu_board.D2
  N3: RELAY_(5V).ground, 5v_(Relay_input).+
  N4: RELAY_(5V).C, AC_switch.1
  N5: RELAY_(5V).NO, AC_Lamp.C
  N6: AC_Lamp.A, AC_switch.2

notes:
  in the Realy
  gnd-input-vcc

custom parts:
  Keyes Relay: The Keyes 5V relay module is suitable for SCM development, home appliance control. It uses a 5V~12V TIL control signal which can control DC / AC signal.
  NodeMCU V3.0: ESP8266 based NodeMCU
  LEDs: LEDs Standard schematic elements and footprints for 5mm, 3mm, 1206, and 0603 sized LEDs. 5mm - Spark Fun Electronics SKU : COM-00529 (and others)
